# Fritzing sketch ControllerCircuit (saved by Fritzing 0.9.3b)
breadboards: 1

parts:
  U2 = NodeMCU V3.0

nets:
  N1: U2.GND#6, U2.GND#13, U2.GND#16, U2.GND#33

custom parts:
  NodeMCU V3.0: ESP8266 based NodeMCU
