# Fritzing sketch EntranceCircuit (saved by Fritzing 0.9.3b)
breadboards: 1

parts:
  U1 = NodeMCU V3.0
  Part1 = RFID-RC522-v3

nets:
  N1: U1.D3, Part1.RST
  N2: U1.D4, Part1.SDA
  3V3: U1.3V3, Part1.3.3V
  N3: U1.GND#6, U1.GND#13, U1.GND#16, U1.GND#33, Part1.GND
  N4: U1.D5, Part1.SCK
  N5: U1.D6, Part1.MISO
  N6: U1.D7, Part1.MOSI

custom parts:
  NodeMCU V3.0: ESP8266 based NodeMCU
  RFID-RC522-v3: A simple China made RFID-RC522 Reader (6x4 cm); do check the pin labels, as this is a MFRC522 based clone.
