# Fritzing sketch Pay-Box (saved by Fritzing 0.9.3b)
breadboards: 1

parts:
  U2 = NodeMCU V3.0
  S1 = Limit Switch [package="Breakout Board"]

nets:
  N1: U2.D4, S1.S
  N2: U2.GND#6, U2.GND#13, U2.GND#16, U2.GND#33, S1.G

notes:
  Any Microswitch

custom parts:
  NodeMCU V3.0: ESP8266 based NodeMCU
  Limit Switch: Generic limit switch commonly found on 3D printers. Typical lever microswitch mounted on a PCB board with a 3 pin JST XH connector.
