# Fritzing sketch RiderCircuit (saved by Fritzing 0.9.3b)
breadboards: 2

parts:
  U2 = NodeMCU V3.0
  Part1 = Arduino Nano (Rev3.0) (ICSP)
  Part2 = Arduino Nano (Rev3.0) (ICSP)
  Part3 = SRF05 Ultrasonic Rangefinder
  Part4 = SRF05 Ultrasonic Rangefinder
  M1 = DC Motor  # not connected
  M2 = DC Motor  # not connected
  M3 = DC Motor  # not connected
  M4 = DC Motor  # not connected
  BAT1 = BC9VPC [package=bc9vpc]
  GY1 = MPU-6050 Board GY-521 [form="♀ (female)" package=THT]
  A1 = A4988
  A2 = A4988
  A3 = A4988
  A4 = A4988
  BAT2 = BC9VPC [package=bc9vpc]
  Part5 = RFID-RC522-v3  # not connected

nets:
  N1: U2.D3, Part1.D7
  N2: U2.D4, Part1.D6
  GND: U2.GND#6, U2.GND#13, U2.GND#16, U2.GND#33, Part1.GND, Part2.GND, BAT1.V-, GY1.pin2, A1.GND#13, A2.GND#13, A3.GND#13, A4.GND#13
  N3: U2.D5, Part2.D7
  N4: U2.D6, Part2.D6
  N5: Part1.D3, Part3.Trig, Part4.Trig
  N6: Part1.D4, Part3.Echo
  N7: Part1.D5, Part4.Echo
  VCC: Part1.VIN, Part3.VCC, Part4.VCC
  VDD: Part2.VIN, A1.VDD, A2.VDD, A3.VDD, A4.VDD
  N8: Part2.A5, GY1.pin3
  N9: Part2.A4, GY1.pin4
  N10: Part2.3V3, GY1.pin1
  GND_2: Part3.GND, Part4.GND
  N11: A1.GND#19, A2.GND#19, A3.GND#19, A4.GND#19, BAT2.V+
  N12: A1.VMOT, A2.VMOT, A3.VMOT, A4.VMOT, BAT2.V-

notes:
  MX1508->
  Arduino Nano1->
  <-Arduino Nano2
  A4988_1
  EN D2
  STEP D3
  DIR D4
  A4988_2
  EN D5
  STEP D8
  DIR D9
  A4988_3
  EN D10
  STEP D11
  DIR D12
  A4988_4
  EN A1
  STEP A2
  DIR A3
  A4988Pins - > Arduino Nano Pins
  Arduino Nano1 Pins -> MFRC522 Pins
  D8 -> RST
  D9 -> SDA(SS)
  D11 -> MOSI
  D12 -> MISO
  D13 - >SCK

custom parts:
  NodeMCU V3.0: ESP8266 based NodeMCU
  MPU-6050 Board GY-521: Acelerometro y Giroscopio MPU-6050 Board GY-521
  RFID-RC522-v3: A simple China made RFID-RC522 Reader (6x4 cm); do check the pin labels, as this is a MFRC522 based clone.
